// Logisim project Digital Vending Machine.circ as structural Verilog: 11 circuits, main circuit Digital Vending Machine
module Digital_Vending_Machine_Circuit (
  input  _1,
  input  _2,
  input  _5,
  input  _10,
  input  Cancel,
  input  Take,
  input  A__2,
  input  B__3,
  input  C__6,
  input  D__8,
  input  E__12,
  input  Restock_A,
  input  Restock_B,
  input  Restock_C,
  input  Restock_D,
  input  Restock_E,
  output out_17,
  output out_18,
  output out_19,
  output out_20,
  output out_21,
  output out_22,
  output out_23,
  output out_24,
  output out_25,
  output out_26,
  output out_27,
  output Dollar,
  output out_29,
  output out_30,
  output out_31,
  output out_32,
  output out_33,
  output out_34,
  output out_35,
  output out_36,
  output out_37,
  output out_38,
  output out_39,
  output out_40,
  output out_41,
  output Dollar_2,
  output out_43,
  output out_44,
  output out_45,
  output out_46,
  output out_47,
  output out_48,
  output out_49,
  output out_50,
  output out_51,
  output out_52,
  output out_53,
  output out_54,
  output out_55,
  output out_56,
  output out_57,
  output out_58,
  output out_59,
  output out_60,
  output out_61,
  output out_62,
  output out_63,
  output out_64,
  output out_65,
  output out_66,
  output out_67,
  output out_68,
  output out_69,
  output out_70,
  output out_71,
  output out_72,
  output out_73,
  output out_74,
  output out_75,
  output out_76,
  output out_77,
  output out_78,
  output out_79,
  output out_80,
  output out_81,
  output out_82,
  output out_83,
  output out_84,
  output out_85,
  output out_86,
  output out_87,
  output out_88,
  output out_89,
  output out_90,
  output out_91,
  output out_92,
  output out_93,
  output out_94,
  output out_95,
  output out_96,
  output out_97,
  output out_98,
  output out_99,
  output out_100,
  output out_101,
  output out_102,
  output out_103,
  output out_104,
  output out_105,
  output out_106,
  output out_107,
  output out_108,
  output out_109,
  output out_110,
  output out_111,
  output out_112,
  output out_113,
  output out_114,
  output out_115,
  output out_116,
  output out_117,
  output out_118,
  output out_119,
  output out_120,
  output out_121,
  output out_122,
  output out_123,
  output out_124,
  output out_125,
  output out_126,
  output out_127,
  output out_128,
  output out_129,
  output out_130,
  output out_131,
  output out_132,
  output out_133,
  output out_134,
  output out_135
);

  wire and_1_out, and_2_out, and_3_out, and_4_out, and_5_out, and_6_out, and_7_out, and_8_out,
       calculation_1_out_9, calculation_1_out_10, calculation_1_out_11, calculation_1_out_12,
       calculation_1_out_13, display_product_1_out_13, display_product_1_out_14, display_product_1_out_15,
       display_product_1_out_16, display_product_1_out_17, insert_money_1_out_7, insert_money_1_out_8,
       insert_money_1_out_9, insert_money_1_out_10, n4_bit_asynchronous_down_counter_1_out_4,
       n4_bit_asynchronous_down_counter_1_out_5, n4_bit_asynchronous_down_counter_1_out_6,
       n4_bit_asynchronous_down_counter_1_out_7, n4_bit_asynchronous_down_counter_1_out_8,
       n4_bit_asynchronous_down_counter_2_out_4, n4_bit_asynchronous_down_counter_2_out_5,
       n4_bit_asynchronous_down_counter_2_out_6, n4_bit_asynchronous_down_counter_2_out_7,
       n4_bit_asynchronous_down_counter_2_out_8, n4_bit_asynchronous_down_counter_3_out_4,
       n4_bit_asynchronous_down_counter_3_out_5, n4_bit_asynchronous_down_counter_3_out_6,
       n4_bit_asynchronous_down_counter_3_out_7, n4_bit_asynchronous_down_counter_3_out_8,
       n4_bit_asynchronous_down_counter_4_out_4, n4_bit_asynchronous_down_counter_4_out_5,
       n4_bit_asynchronous_down_counter_4_out_6, n4_bit_asynchronous_down_counter_4_out_7,
       n4_bit_asynchronous_down_counter_4_out_8, n4_bit_asynchronous_down_counter_5_out_4,
       n4_bit_asynchronous_down_counter_5_out_5, n4_bit_asynchronous_down_counter_5_out_6,
       n4_bit_asynchronous_down_counter_5_out_7, n4_bit_asynchronous_down_counter_5_out_8, not_1_out,
       not_2_out, or_1_out, or_2_out, product_selection_1_out_8, product_selection_1_out_9,
       product_selection_1_out_10, product_selection_1_out_11;

  and and_1 (and_1_out, not_1_out, Cancel);
  _4_bit_Asynchronous_Down_Counter u_4_bit_asynchronous_down_counter_1 (
    .Clock(and_4_out), .Preset(Restock_A), .out_4(n4_bit_asynchronous_down_counter_1_out_4),
    .out_5(n4_bit_asynchronous_down_counter_1_out_5), .out_6(n4_bit_asynchronous_down_counter_1_out_6),
    .out_7(n4_bit_asynchronous_down_counter_1_out_7), .out_8(n4_bit_asynchronous_down_counter_1_out_8),
    .Disable(display_product_1_out_13));
  and and_2 (and_2_out, A__2, n4_bit_asynchronous_down_counter_1_out_8);
  and and_3 (and_3_out, B__3, n4_bit_asynchronous_down_counter_2_out_8);
  _4_bit_Asynchronous_Down_Counter u_4_bit_asynchronous_down_counter_2 (
    .Clock(and_4_out), .Preset(Restock_B), .out_4(n4_bit_asynchronous_down_counter_2_out_4),
    .out_5(n4_bit_asynchronous_down_counter_2_out_5), .out_6(n4_bit_asynchronous_down_counter_2_out_6),
    .out_7(n4_bit_asynchronous_down_counter_2_out_7), .out_8(n4_bit_asynchronous_down_counter_2_out_8),
    .Disable(display_product_1_out_14));
  _4_bit_Asynchronous_Down_Counter u_4_bit_asynchronous_down_counter_3 (
    .Clock(and_4_out), .Preset(Restock_C), .out_4(n4_bit_asynchronous_down_counter_3_out_4),
    .out_5(n4_bit_asynchronous_down_counter_3_out_5), .out_6(n4_bit_asynchronous_down_counter_3_out_6),
    .out_7(n4_bit_asynchronous_down_counter_3_out_7), .out_8(n4_bit_asynchronous_down_counter_3_out_8),
    .Disable(display_product_1_out_15));
  and and_4 (and_4_out, and_8_out, Take);
  and and_5 (and_5_out, C__6, n4_bit_asynchronous_down_counter_3_out_8);
  _4_bit_Asynchronous_Down_Counter u_4_bit_asynchronous_down_counter_4 (
    .Clock(and_4_out), .Preset(Restock_D), .out_4(n4_bit_asynchronous_down_counter_4_out_4),
    .out_5(n4_bit_asynchronous_down_counter_4_out_5), .out_6(n4_bit_asynchronous_down_counter_4_out_6),
    .out_7(n4_bit_asynchronous_down_counter_4_out_7), .out_8(n4_bit_asynchronous_down_counter_4_out_8),
    .Disable(display_product_1_out_16));
  and and_6 (and_6_out, D__8, n4_bit_asynchronous_down_counter_4_out_8);
  and and_7 (and_7_out, E__12, n4_bit_asynchronous_down_counter_5_out_8);
  _4_bit_Asynchronous_Down_Counter u_4_bit_asynchronous_down_counter_5 (
    .Clock(and_4_out), .Preset(Restock_E), .out_4(n4_bit_asynchronous_down_counter_5_out_4),
    .out_5(n4_bit_asynchronous_down_counter_5_out_5), .out_6(n4_bit_asynchronous_down_counter_5_out_6),
    .out_7(n4_bit_asynchronous_down_counter_5_out_7), .out_8(n4_bit_asynchronous_down_counter_5_out_8),
    .Disable(display_product_1_out_17));
  Insert_Money insert_money_1 (
    ._1(_1), ._2(_2), ._5(_5), ._10(_10), .out_7(insert_money_1_out_7), .out_8(insert_money_1_out_8),
    .out_9(insert_money_1_out_9), .out_10(insert_money_1_out_10), .Clear(or_1_out), .Disable(and_8_out));
  or or_1 (or_1_out, and_1_out, and_4_out);
  Product_Selection product_selection_1 (
    .out_8(product_selection_1_out_8), .out_9(product_selection_1_out_9),
    .out_10(product_selection_1_out_10), .out_11(product_selection_1_out_11), ._2(and_2_out), ._3(and_3_out),
    ._6(and_5_out), ._8(and_6_out), ._12(and_7_out), .Clear(or_1_out), .Disable(and_8_out));
  _4_bit_binary_to_7_segment_display u_4_bit_binary_to_7_segment_display_1 (
    .in_1(n4_bit_asynchronous_down_counter_1_out_7), .in_3(n4_bit_asynchronous_down_counter_1_out_6),
    .in_4(n4_bit_asynchronous_down_counter_1_out_5), .in_5(n4_bit_asynchronous_down_counter_1_out_4),
    .out_6(out_47), .out_7(out_48), .out_8(out_55), .out_9(out_54), .out_10(out_53), .out_11(out_46),
    .out_12(out_45), .out_13(out_51), .out_14(out_52), .out_15(out_58), .out_16(out_57), .out_17(out_56),
    .out_18(out_50), .out_19(out_49), .in_2(1'b1));
  _4_bit_binary_to_7_segment_display u_4_bit_binary_to_7_segment_display_2 (
    .in_1(n4_bit_asynchronous_down_counter_2_out_7), .in_3(n4_bit_asynchronous_down_counter_2_out_6),
    .in_4(n4_bit_asynchronous_down_counter_2_out_5), .in_5(n4_bit_asynchronous_down_counter_2_out_4),
    .out_6(out_61), .out_7(out_62), .out_8(out_69), .out_9(out_68), .out_10(out_67), .out_11(out_60),
    .out_12(out_59), .out_13(out_65), .out_14(out_66), .out_15(out_72), .out_16(out_71), .out_17(out_70),
    .out_18(out_64), .out_19(out_63), .in_2(1'b1));
  _4_bit_binary_to_7_segment_display u_4_bit_binary_to_7_segment_display_3 (
    .in_1(n4_bit_asynchronous_down_counter_3_out_7), .in_3(n4_bit_asynchronous_down_counter_3_out_6),
    .in_4(n4_bit_asynchronous_down_counter_3_out_5), .in_5(n4_bit_asynchronous_down_counter_3_out_4),
    .out_6(out_75), .out_7(out_76), .out_8(out_95), .out_9(out_94), .out_10(out_93), .out_11(out_74),
    .out_12(out_73), .out_13(out_79), .out_14(out_80), .out_15(out_98), .out_16(out_97), .out_17(out_96),
    .out_18(out_78), .out_19(out_77), .in_2(1'b1));
  _4_bit_binary_to_7_segment_display u_4_bit_binary_to_7_segment_display_4 (
    .in_1(n4_bit_asynchronous_down_counter_4_out_7), .in_3(n4_bit_asynchronous_down_counter_4_out_6),
    .in_4(n4_bit_asynchronous_down_counter_4_out_5), .in_5(n4_bit_asynchronous_down_counter_4_out_4),
    .out_6(out_101), .out_7(out_102), .out_8(out_118), .out_9(out_117), .out_10(out_116), .out_11(out_100),
    .out_12(out_99), .out_13(out_105), .out_14(out_106), .out_15(out_121), .out_16(out_120),
    .out_17(out_119), .out_18(out_104), .out_19(out_103), .in_2(1'b1));
  _4_bit_binary_to_7_segment_display u_4_bit_binary_to_7_segment_display_5 (
    .in_1(n4_bit_asynchronous_down_counter_5_out_7), .in_3(n4_bit_asynchronous_down_counter_5_out_6),
    .in_4(n4_bit_asynchronous_down_counter_5_out_5), .in_5(n4_bit_asynchronous_down_counter_5_out_4),
    .out_6(out_124), .out_7(out_125), .out_8(out_132), .out_9(out_131), .out_10(out_130), .out_11(out_123),
    .out_12(out_122), .out_13(out_128), .out_14(out_129), .out_15(out_135), .out_16(out_134),
    .out_17(out_133), .out_18(out_127), .out_19(out_126), .in_2(1'b1));
  Display_Product display_product_1 (
    .in_1(product_selection_1_out_8), .in_3(product_selection_1_out_9), .in_4(product_selection_1_out_10),
    .in_5(product_selection_1_out_11), .out_6(out_83), .out_7(out_84), .out_8(out_109), .out_9(out_108),
    .out_10(out_107), .out_11(out_82), .out_12(out_81), .in_2(and_8_out), .out_13(display_product_1_out_13),
    .out_14(display_product_1_out_14), .out_15(display_product_1_out_15), .out_16(display_product_1_out_16),
    .out_17(display_product_1_out_17));
  or or_2 (or_2_out, product_selection_1_out_8, product_selection_1_out_9, product_selection_1_out_10, product_selection_1_out_11);
  Calculation calculation_1 (
    .in_5(product_selection_1_out_8), .Price(product_selection_1_out_9), .in_7(product_selection_1_out_10),
    .in_8(product_selection_1_out_11), .out_9(calculation_1_out_9), .out_10(calculation_1_out_10),
    .out_11(calculation_1_out_11), .out_12(calculation_1_out_12), .out_13(calculation_1_out_13),
    .in_1(insert_money_1_out_7), .Money(insert_money_1_out_8), .in_3(insert_money_1_out_9),
    .in_4(insert_money_1_out_10));
  and and_8 (and_8_out, or_2_out, calculation_1_out_9);
  not not_1 (not_1_out, and_8_out);
  not not_2 (not_2_out, calculation_1_out_9);
  _4_bit_binary_to_7_segment_display u_4_bit_binary_to_7_segment_display_6 (
    .in_1(insert_money_1_out_7), .in_3(insert_money_1_out_8), .in_4(insert_money_1_out_9),
    .in_5(insert_money_1_out_10), .out_6(out_19), .out_7(out_20), .out_8(out_27), .out_9(out_26),
    .out_10(out_25), .out_11(out_18), .out_12(out_17), .out_13(out_23), .out_14(out_24), .out_15(out_30),
    .out_16(out_29), .out_17(Dollar), .out_18(out_22), .out_19(out_21), .in_2(not_1_out));
  _4_bit_binary_to_7_segment_display u_4_bit_binary_to_7_segment_display_7 (
    .in_1(calculation_1_out_10), .in_3(calculation_1_out_11), .in_4(calculation_1_out_12),
    .in_5(calculation_1_out_13), .out_6(out_33), .out_7(out_34), .out_8(out_41), .out_9(out_40),
    .out_10(out_39), .out_11(out_32), .out_12(out_31), .out_13(out_37), .out_14(out_38), .out_15(out_44),
    .out_16(out_43), .out_17(Dollar_2), .out_18(out_36), .out_19(out_35), .in_2(not_2_out));
  _4_bit_binary_to_7_segment_display u_4_bit_binary_to_7_segment_display_8 (
    .in_1(calculation_1_out_10), .in_3(calculation_1_out_11), .in_4(calculation_1_out_12),
    .in_5(calculation_1_out_13), .out_6(out_87), .out_7(out_88), .out_8(out_112), .out_9(out_111),
    .out_10(out_110), .out_11(out_86), .out_12(out_85), .out_13(out_91), .out_14(out_92), .out_15(out_115),
    .out_16(out_114), .out_17(out_113), .out_18(out_90), .out_19(out_89), .in_2(and_8_out));

  // Notes on the sheet:
  //   Product
  //   Inserted
  //   Needed
  //   Return
endmodule

module Insert_Money (
  input  Clear,
  input  Disable,
  input  _1,
  input  _2,
  input  _5,
  input  _10,
  output out_7,
  output out_8,
  output out_9,
  output out_10
);

  wire LSB_out, n4_bit_adder_subtractor_1_out_10, n4_bit_adder_subtractor_1_out_11,
       n4_bit_adder_subtractor_1_out_12, n4_bit_adder_subtractor_1_out_13, n4_bit_adder_subtractor_1_out_14,
       nor_1_out, or_1_out, or_2_out;

  or or_1 (or_1_out, _10, _2);
  or LSB (LSB_out, _5, _1);
  nor nor_1 (nor_1_out, _10, _5, _2, _1);
  _4_Bit_Adder_Subtractor u_4_bit_adder_subtractor_1 (
    .in_1(1'b0), .in_2(_10), .in_3(out_7), .in_4(_5), .in_5(out_8), .in_6(or_1_out), .in_7(out_9),
    .in_8(LSB_out), .in_9(out_10), .out_10(n4_bit_adder_subtractor_1_out_10),
    .out_11(n4_bit_adder_subtractor_1_out_11), .out_12(n4_bit_adder_subtractor_1_out_12),
    .out_13(n4_bit_adder_subtractor_1_out_13), .out_14(n4_bit_adder_subtractor_1_out_14));
  _4_bit_memory u_4_bit_memory_1 (
    .in_3(n4_bit_adder_subtractor_1_out_11), .in_4(n4_bit_adder_subtractor_1_out_12),
    .in_5(n4_bit_adder_subtractor_1_out_13), .in_6(n4_bit_adder_subtractor_1_out_14), .out_8(out_7),
    .out_9(out_8), .out_10(out_9), .out_11(out_10), .Clear(Clear), .Clk(nor_1_out), .Disabled(or_2_out));
  or or_2 (or_2_out, n4_bit_adder_subtractor_1_out_10, Disable);
endmodule

module _4_bit_binary_to_7_segment_display (
  input  in_1,
  input  in_2,
  input  in_3,
  input  in_4,
  input  in_5,
  output out_6,
  output out_7,
  output out_8,
  output out_9,
  output out_10,
  output out_11,
  output out_12,
  output out_13,
  output out_14,
  output out_15,
  output out_16,
  output out_17,
  output out_18,
  output out_19
);

  wire _0_out, _1_out, _2_out, _3_out, _4_out, _5_out, _6_out, _7_out, _8_out, _10_out, _11_out, _12_out,
       _13_out, _14_out, _15_out, nor_1_out, nor_2_out, nor_3_out, nor_4_out, nor_5_out, nor_6_out,
       nor_7_out, not_1_out, not_2_out, not_3_out, not_4_out, or_1_out;

  not not_1 (not_1_out, in_1);
  not not_2 (not_2_out, in_3);
  not not_3 (not_3_out, in_4);
  not not_4 (not_4_out, in_5);
  and _0 (_0_out, not_1_out, not_2_out, not_3_out, not_4_out);
  and _1 (_1_out, not_1_out, not_2_out, not_3_out, in_5);
  and _2 (_2_out, not_1_out, not_2_out, in_4, not_4_out);
  and _3 (_3_out, not_1_out, not_2_out, in_4, in_5);
  and _5 (_5_out, not_1_out, in_3, not_3_out, in_5);
  and _4 (_4_out, not_1_out, in_3, not_3_out, not_4_out);
  and _6 (_6_out, not_1_out, in_3, in_4, not_4_out);
  and _7 (_7_out, not_1_out, in_3, in_4, in_5);
  and _8 (_8_out, in_1, not_2_out, not_3_out, not_4_out);
  // AND_Gate _9 has open pins: in0=in_1, in1=not_2_out, in2=not_3_out, in3=in_5, out=open
  and _10 (_10_out, in_1, not_2_out, in_4, not_4_out);
  and _11 (_11_out, in_1, not_2_out, in_4, in_5);
  and _13 (_13_out, in_1, in_3, not_3_out, in_5);
  and _12 (_12_out, in_1, in_3, not_3_out, not_4_out);
  and _14 (_14_out, in_1, in_3, in_4, not_4_out);
  and _15 (_15_out, in_1, in_3, in_4, in_5);
  or or_1 (or_1_out, _12_out, _10_out, _8_out, _6_out, _2_out, _0_out);
  nor nor_1 (nor_1_out, _15_out, _14_out, _13_out, _12_out, _11_out, _10_out);
  nor nor_2 (nor_2_out, _14_out, _11_out, _4_out, _1_out);
  nor nor_3 (nor_3_out, _15_out, _6_out, _5_out);
  nor nor_4 (nor_4_out, _12_out, _2_out);
  nor nor_5 (nor_5_out, _14_out, _11_out, _7_out, _4_out, _1_out);
  nor nor_6 (nor_6_out, _13_out, _12_out, _11_out, _7_out, _3_out, _2_out, _1_out);
  nor nor_7 (nor_7_out, _11_out, _10_out, _7_out, _1_out, _0_out);
  and and_1 (out_6, in_2, nor_1_out);
  and and_2 (out_7, in_2, 1'b1);
  and and_3 (out_8, in_2, 1'b1);
  and and_4 (out_9, in_2, nor_1_out);
  and and_5 (out_10, in_2, nor_1_out);
  and and_6 (out_11, in_2, nor_1_out);
  and and_7 (out_12, in_2, 1'b0);
  and and_8 (out_13, in_2, nor_2_out);
  and and_9 (out_14, in_2, nor_3_out);
  and and_10 (out_15, in_2, nor_4_out);
  and and_11 (out_16, in_2, nor_5_out);
  and and_12 (out_17, in_2, or_1_out);
  and and_13 (out_18, in_2, nor_6_out);
  and and_14 (out_19, in_2, nor_7_out);
endmodule

module Product_Selection (
  input  Disable,
  input  _2,
  input  _3,
  input  _6,
  input  _8,
  input  _12,
  input  Clear,
  output out_8,
  output out_9,
  output out_10,
  output out_11
);

  wire MSB_out, or_1_out, or_2_out, or_3_out;

  or MSB (MSB_out, _12, _8);
  or or_1 (or_1_out, _12, _6);
  or or_2 (or_2_out, _6, _3, _2);
  or or_3 (or_3_out, _12, _8, _6, _3, _2);
  _4_bit_memory u_4_bit_memory_1 (
    .in_3(MSB_out), .in_4(or_1_out), .in_5(or_2_out), .in_6(_3), .out_8(out_8), .out_9(out_9),
    .out_10(out_10), .out_11(out_11), .Clear(Clear), .Clk(or_3_out), .Disabled(Disable));
endmodule

module _4_Bit_Comparator (
  input  A,
  input  B,
  input  A_2,
  input  B_2,
  input  A_3,
  input  B_3,
  input  A_4,
  input  B_4,
  output out_9
);

  wire A_B_out, and_1_out, and_2_out, and_3_out, and_4_out, and_5_out, and_6_out, and_7_out, and_8_out,
       and_9_out, and_10_out, and_11_out, and_12_out, nor_1_out, nor_2_out, nor_3_out, nor_4_out, not_1_out,
       not_2_out, not_3_out, not_4_out, not_5_out, not_6_out, not_7_out, not_8_out;

  not not_1 (not_1_out, A);
  not not_2 (not_2_out, B);
  not not_3 (not_3_out, A_2);
  not not_4 (not_4_out, B_2);
  not not_5 (not_5_out, A_3);
  not not_6 (not_6_out, B_3);
  not not_7 (not_7_out, A_4);
  not not_8 (not_8_out, B_4);
  and and_1 (and_1_out, not_1_out, B);
  and and_2 (and_2_out, A, not_2_out);
  and and_3 (and_3_out, not_3_out, B_2);
  and and_4 (and_4_out, A_2, not_4_out);
  and and_5 (and_5_out, not_5_out, B_3);
  and and_6 (and_6_out, A_3, not_6_out);
  and and_7 (and_7_out, not_7_out, B_4);
  and and_8 (and_8_out, A_4, not_8_out);
  nor nor_1 (nor_1_out, and_1_out, and_2_out);
  nor nor_2 (nor_2_out, and_3_out, and_4_out);
  nor nor_3 (nor_3_out, and_5_out, and_6_out);
  nor nor_4 (nor_4_out, and_7_out, and_8_out);
  and and_9 (and_9_out, nor_1_out, and_4_out);
  and and_10 (and_10_out, nor_1_out, nor_2_out, and_6_out);
  and and_11 (and_11_out, nor_1_out, nor_2_out, nor_3_out, and_8_out);
  and and_12 (and_12_out, nor_1_out, nor_2_out, nor_3_out, nor_4_out);
  or A_B (A_B_out, and_2_out, and_9_out, and_10_out, and_11_out);
  or A__B (out_9, A_B_out, and_12_out);

  // Notes on the sheet:
  //   MSB
  //   LSB
endmodule

module _4_Bit_Adder_Subtractor (
  input  in_1,
  input  in_2,
  input  in_3,
  input  in_4,
  input  in_5,
  input  in_6,
  input  in_7,
  input  in_8,
  input  in_9,
  output out_10,
  output out_11,
  output out_12,
  output out_13,
  output out_14
);

  wire adder_2_cout, adder_3_cout, adder_4_cout, xor_1_out, xor_2_out, xor_3_out, xor_4_out;

  xor xor_1 (xor_1_out, in_1, in_3);
  xor xor_2 (xor_2_out, in_1, in_5);
  xor xor_3 (xor_3_out, in_1, in_7);
  xor xor_4 (xor_4_out, in_1, in_9);
  Adder #(.width(1)) adder_1 (.a(in_2), .b(xor_1_out), .out(out_11), .cin(adder_2_cout), .cout(out_10));
  Adder #(.width(1)) adder_2 (.a(in_4), .b(xor_2_out), .out(out_12), .cin(adder_3_cout), .cout(adder_2_cout));
  Adder #(.width(1)) adder_3 (.a(in_6), .b(xor_3_out), .out(out_13), .cin(adder_4_cout), .cout(adder_3_cout));
  Adder #(.width(1)) adder_4 (.a(in_8), .b(xor_4_out), .out(out_14), .cin(in_1), .cout(adder_4_cout));
endmodule

module _4_bit_memory (
  input  Disabled,
  input  Clear,
  input  in_3,
  input  in_4,
  input  in_5,
  input  in_6,
  input  Clk,
  output out_8,
  output out_9,
  output out_10,
  output out_11
);

  wire not_1_out;

  not not_1 (not_1_out, Disabled);
  D_Flip_Flop d_ff_1 (.clk(Clk), .D(in_3), .Q(out_8), .en(not_1_out), .reset(Clear));  // open: Qn, preset
  D_Flip_Flop d_ff_2 (.clk(Clk), .D(in_4), .Q(out_9), .en(not_1_out), .reset(Clear));  // open: Qn, preset
  D_Flip_Flop d_ff_3 (.clk(Clk), .D(in_5), .Q(out_10), .en(not_1_out), .reset(Clear));  // open: Qn, preset
  D_Flip_Flop d_ff_4 (.clk(Clk), .D(in_6), .Q(out_11), .en(not_1_out), .reset(Clear));  // open: Qn, preset
endmodule

module Calculation (
  input  in_1,
  input  Money,
  input  in_3,
  input  in_4,
  input  in_5,
  input  Price,
  input  in_7,
  input  in_8,
  output out_9,
  output out_10,
  output out_11,
  output out_12,
  output out_13
);

  wire n4_bit_adder_subtractor_1_out_10, n4_bit_adder_subtractor_1_out_11, n4_bit_adder_subtractor_1_out_12,
       n4_bit_adder_subtractor_1_out_13, n4_bit_adder_subtractor_1_out_14, not_1_out, not_2_out;

  _4_Bit_Comparator u_4_bit_comparator_1 (
    .A(in_1), .B(in_5), .A_2(Money), .B_2(Price), .A_3(in_3), .B_3(in_7), .A_4(in_4), .B_4(in_8),
    .out_9(out_9));
  _4_Bit_Adder_Subtractor u_4_bit_adder_subtractor_1 (
    .in_1(1'b1), .in_2(in_1), .in_3(in_5), .in_4(Money), .in_5(Price), .in_6(in_3), .in_7(in_7), .in_8(in_4),
    .in_9(in_8), .out_10(n4_bit_adder_subtractor_1_out_10), .out_11(n4_bit_adder_subtractor_1_out_11),
    .out_12(n4_bit_adder_subtractor_1_out_12), .out_13(n4_bit_adder_subtractor_1_out_13),
    .out_14(n4_bit_adder_subtractor_1_out_14));
  not not_1 (not_1_out, 1'b1);
  _4_Bit_Adder_Subtractor u_4_bit_adder_subtractor_2 (
    .in_1(not_2_out), .in_2(not_1_out), .in_3(n4_bit_adder_subtractor_1_out_11), .in_4(not_1_out),
    .in_5(n4_bit_adder_subtractor_1_out_12), .in_6(not_1_out), .in_7(n4_bit_adder_subtractor_1_out_13),
    .in_8(not_1_out), .in_9(n4_bit_adder_subtractor_1_out_14), .out_11(out_10), .out_12(out_11),
    .out_13(out_12), .out_14(out_13));  // open: out_10
  not not_2 (not_2_out, n4_bit_adder_subtractor_1_out_10);
endmodule

module Display_Product (
  input  in_1,
  input  in_2,
  input  in_3,
  input  in_4,
  input  in_5,
  output out_6,
  output out_7,
  output out_8,
  output out_9,
  output out_10,
  output out_11,
  output out_12,
  output out_13,
  output out_14,
  output out_15,
  output out_16,
  output out_17
);

  wire nor_1_out, nor_2_out, not_1_out, not_2_out, not_3_out, not_4_out, not_5_out;

  not not_1 (not_1_out, in_1);
  not not_2 (not_2_out, in_3);
  not not_3 (not_3_out, in_4);
  not not_4 (not_4_out, in_5);
  and _2 (out_13, not_1_out, not_2_out, in_4, not_4_out);
  and _3 (out_14, not_1_out, not_2_out, in_4, in_5);
  and _6 (out_15, not_1_out, in_3, in_4, not_4_out);
  and _8 (out_16, in_1, not_2_out, not_3_out, not_4_out);
  and _12 (out_17, in_1, in_3, not_3_out, not_4_out);
  nor nor_1 (nor_1_out, out_17, out_15);
  not not_5 (not_5_out, out_13);
  nor nor_2 (nor_2_out, out_16, out_15);
  and and_1 (out_7, in_2, nor_1_out);
  and and_2 (out_8, in_2, nor_1_out);
  and and_3 (out_9, in_2, not_5_out);
  and and_4 (out_12, in_2, nor_2_out);

  assign out_6 = in_2;
  assign out_10 = in_2;
  assign out_11 = in_2;
endmodule

module Digital_Vending_Machine (
);

  wire _1_out, _2_out, _5_out, _10_out, A__2_out, B__3_out, C__6_out, Cancel_out, D__8_out,
       digital_vending_machine_circuit_1_dollar, digital_vending_machine_circuit_1_dollar_2,
       digital_vending_machine_circuit_1_out_17, digital_vending_machine_circuit_1_out_18,
       digital_vending_machine_circuit_1_out_19, digital_vending_machine_circuit_1_out_20,
       digital_vending_machine_circuit_1_out_21, digital_vending_machine_circuit_1_out_22,
       digital_vending_machine_circuit_1_out_23, digital_vending_machine_circuit_1_out_24,
       digital_vending_machine_circuit_1_out_25, digital_vending_machine_circuit_1_out_26,
       digital_vending_machine_circuit_1_out_27, digital_vending_machine_circuit_1_out_29,
       digital_vending_machine_circuit_1_out_30, digital_vending_machine_circuit_1_out_31,
       digital_vending_machine_circuit_1_out_32, digital_vending_machine_circuit_1_out_33,
       digital_vending_machine_circuit_1_out_34, digital_vending_machine_circuit_1_out_35,
       digital_vending_machine_circuit_1_out_36, digital_vending_machine_circuit_1_out_37,
       digital_vending_machine_circuit_1_out_38, digital_vending_machine_circuit_1_out_39,
       digital_vending_machine_circuit_1_out_40, digital_vending_machine_circuit_1_out_41,
       digital_vending_machine_circuit_1_out_43, digital_vending_machine_circuit_1_out_44,
       digital_vending_machine_circuit_1_out_45, digital_vending_machine_circuit_1_out_46,
       digital_vending_machine_circuit_1_out_47, digital_vending_machine_circuit_1_out_48,
       digital_vending_machine_circuit_1_out_49, digital_vending_machine_circuit_1_out_50,
       digital_vending_machine_circuit_1_out_51, digital_vending_machine_circuit_1_out_52,
       digital_vending_machine_circuit_1_out_53, digital_vending_machine_circuit_1_out_54,
       digital_vending_machine_circuit_1_out_55, digital_vending_machine_circuit_1_out_56,
       digital_vending_machine_circuit_1_out_57, digital_vending_machine_circuit_1_out_58,
       digital_vending_machine_circuit_1_out_59, digital_vending_machine_circuit_1_out_60,
       digital_vending_machine_circuit_1_out_61, digital_vending_machine_circuit_1_out_62,
       digital_vending_machine_circuit_1_out_63, digital_vending_machine_circuit_1_out_64,
       digital_vending_machine_circuit_1_out_65, digital_vending_machine_circuit_1_out_66,
       digital_vending_machine_circuit_1_out_67, digital_vending_machine_circuit_1_out_68,
       digital_vending_machine_circuit_1_out_69, digital_vending_machine_circuit_1_out_70,
       digital_vending_machine_circuit_1_out_71, digital_vending_machine_circuit_1_out_72,
       digital_vending_machine_circuit_1_out_73, digital_vending_machine_circuit_1_out_74,
       digital_vending_machine_circuit_1_out_75, digital_vending_machine_circuit_1_out_76,
       digital_vending_machine_circuit_1_out_77, digital_vending_machine_circuit_1_out_78,
       digital_vending_machine_circuit_1_out_79, digital_vending_machine_circuit_1_out_80,
       digital_vending_machine_circuit_1_out_81, digital_vending_machine_circuit_1_out_82,
       digital_vending_machine_circuit_1_out_83, digital_vending_machine_circuit_1_out_84,
       digital_vending_machine_circuit_1_out_85, digital_vending_machine_circuit_1_out_86,
       digital_vending_machine_circuit_1_out_87, digital_vending_machine_circuit_1_out_88,
       digital_vending_machine_circuit_1_out_89, digital_vending_machine_circuit_1_out_90,
       digital_vending_machine_circuit_1_out_91, digital_vending_machine_circuit_1_out_92,
       digital_vending_machine_circuit_1_out_93, digital_vending_machine_circuit_1_out_94,
       digital_vending_machine_circuit_1_out_95, digital_vending_machine_circuit_1_out_96,
       digital_vending_machine_circuit_1_out_97, digital_vending_machine_circuit_1_out_98,
       digital_vending_machine_circuit_1_out_99, digital_vending_machine_circuit_1_out_100,
       digital_vending_machine_circuit_1_out_101, digital_vending_machine_circuit_1_out_102,
       digital_vending_machine_circuit_1_out_103, digital_vending_machine_circuit_1_out_104,
       digital_vending_machine_circuit_1_out_105, digital_vending_machine_circuit_1_out_106,
       digital_vending_machine_circuit_1_out_107, digital_vending_machine_circuit_1_out_108,
       digital_vending_machine_circuit_1_out_109, digital_vending_machine_circuit_1_out_110,
       digital_vending_machine_circuit_1_out_111, digital_vending_machine_circuit_1_out_112,
       digital_vending_machine_circuit_1_out_113, digital_vending_machine_circuit_1_out_114,
       digital_vending_machine_circuit_1_out_115, digital_vending_machine_circuit_1_out_116,
       digital_vending_machine_circuit_1_out_117, digital_vending_machine_circuit_1_out_118,
       digital_vending_machine_circuit_1_out_119, digital_vending_machine_circuit_1_out_120,
       digital_vending_machine_circuit_1_out_121, digital_vending_machine_circuit_1_out_122,
       digital_vending_machine_circuit_1_out_123, digital_vending_machine_circuit_1_out_124,
       digital_vending_machine_circuit_1_out_125, digital_vending_machine_circuit_1_out_126,
       digital_vending_machine_circuit_1_out_127, digital_vending_machine_circuit_1_out_128,
       digital_vending_machine_circuit_1_out_129, digital_vending_machine_circuit_1_out_130,
       digital_vending_machine_circuit_1_out_131, digital_vending_machine_circuit_1_out_132,
       digital_vending_machine_circuit_1_out_133, digital_vending_machine_circuit_1_out_134,
       digital_vending_machine_circuit_1_out_135, E__12_out, Restock_A_out, Restock_B_out, Restock_C_out,
       Restock_D_out, Restock_E_out, Take_Return___Product_out;

  Button Restock_A (.out(Restock_A_out));
  Button Restock_B (.out(Restock_B_out));
  Button Restock_C (.out(Restock_C_out));
  Button Restock_D (.out(Restock_D_out));
  Button Restock_E (.out(Restock_E_out));
  _7_Segment_Display u_7_segment_display_1 (
    .g(digital_vending_machine_circuit_1_out_45), .f(digital_vending_machine_circuit_1_out_46),
    .a(digital_vending_machine_circuit_1_out_47), .b(digital_vending_machine_circuit_1_out_48),
    .e(digital_vending_machine_circuit_1_out_53), .d(digital_vending_machine_circuit_1_out_54),
    .c(digital_vending_machine_circuit_1_out_55));  // open: dp
  _7_Segment_Display u_7_segment_display_2 (
    .g(digital_vending_machine_circuit_1_out_59), .f(digital_vending_machine_circuit_1_out_60),
    .a(digital_vending_machine_circuit_1_out_61), .b(digital_vending_machine_circuit_1_out_62),
    .e(digital_vending_machine_circuit_1_out_67), .d(digital_vending_machine_circuit_1_out_68),
    .c(digital_vending_machine_circuit_1_out_69));  // open: dp
  _7_Segment_Display u_7_segment_display_3 (
    .g(digital_vending_machine_circuit_1_out_73), .f(digital_vending_machine_circuit_1_out_74),
    .a(digital_vending_machine_circuit_1_out_75), .b(digital_vending_machine_circuit_1_out_76),
    .e(digital_vending_machine_circuit_1_out_93), .d(digital_vending_machine_circuit_1_out_94),
    .c(digital_vending_machine_circuit_1_out_95));  // open: dp
  _7_Segment_Display u_7_segment_display_4 (
    .g(digital_vending_machine_circuit_1_out_99), .f(digital_vending_machine_circuit_1_out_100),
    .a(digital_vending_machine_circuit_1_out_101), .b(digital_vending_machine_circuit_1_out_102),
    .e(digital_vending_machine_circuit_1_out_116), .d(digital_vending_machine_circuit_1_out_117),
    .c(digital_vending_machine_circuit_1_out_118));  // open: dp
  _7_Segment_Display u_7_segment_display_5 (
    .g(digital_vending_machine_circuit_1_out_122), .f(digital_vending_machine_circuit_1_out_123),
    .a(digital_vending_machine_circuit_1_out_124), .b(digital_vending_machine_circuit_1_out_125),
    .e(digital_vending_machine_circuit_1_out_130), .d(digital_vending_machine_circuit_1_out_131),
    .c(digital_vending_machine_circuit_1_out_132));  // open: dp
  _7_Segment_Display u_7_segment_display_6 (
    .g(digital_vending_machine_circuit_1_out_81), .f(digital_vending_machine_circuit_1_out_82),
    .a(digital_vending_machine_circuit_1_out_83), .b(digital_vending_machine_circuit_1_out_84),
    .e(digital_vending_machine_circuit_1_out_107), .d(digital_vending_machine_circuit_1_out_108),
    .c(digital_vending_machine_circuit_1_out_109));  // open: dp
  Digital_Vending_Machine_Circuit digital_vending_machine_circuit_1 (
    ._1(_1_out), ._2(_2_out), ._5(_5_out), ._10(_10_out), .Cancel(Cancel_out),
    .Take(Take_Return___Product_out), .A__2(A__2_out), .B__3(B__3_out), .C__6(C__6_out), .D__8(D__8_out),
    .E__12(E__12_out), .Restock_A(Restock_A_out), .Restock_B(Restock_B_out), .Restock_C(Restock_C_out),
    .Restock_D(Restock_D_out), .Restock_E(Restock_E_out), .out_17(digital_vending_machine_circuit_1_out_17),
    .out_18(digital_vending_machine_circuit_1_out_18), .out_19(digital_vending_machine_circuit_1_out_19),
    .out_20(digital_vending_machine_circuit_1_out_20), .out_25(digital_vending_machine_circuit_1_out_25),
    .out_26(digital_vending_machine_circuit_1_out_26), .out_27(digital_vending_machine_circuit_1_out_27),
    .out_21(digital_vending_machine_circuit_1_out_21), .out_22(digital_vending_machine_circuit_1_out_22),
    .out_23(digital_vending_machine_circuit_1_out_23), .out_24(digital_vending_machine_circuit_1_out_24),
    .Dollar(digital_vending_machine_circuit_1_dollar), .out_29(digital_vending_machine_circuit_1_out_29),
    .out_30(digital_vending_machine_circuit_1_out_30), .out_31(digital_vending_machine_circuit_1_out_31),
    .out_32(digital_vending_machine_circuit_1_out_32), .out_33(digital_vending_machine_circuit_1_out_33),
    .out_34(digital_vending_machine_circuit_1_out_34), .out_35(digital_vending_machine_circuit_1_out_35),
    .out_36(digital_vending_machine_circuit_1_out_36), .out_37(digital_vending_machine_circuit_1_out_37),
    .out_38(digital_vending_machine_circuit_1_out_38), .out_39(digital_vending_machine_circuit_1_out_39),
    .out_40(digital_vending_machine_circuit_1_out_40), .out_41(digital_vending_machine_circuit_1_out_41),
    .Dollar_2(digital_vending_machine_circuit_1_dollar_2), .out_43(digital_vending_machine_circuit_1_out_43),
    .out_44(digital_vending_machine_circuit_1_out_44), .out_81(digital_vending_machine_circuit_1_out_81),
    .out_82(digital_vending_machine_circuit_1_out_82), .out_83(digital_vending_machine_circuit_1_out_83),
    .out_84(digital_vending_machine_circuit_1_out_84), .out_107(digital_vending_machine_circuit_1_out_107),
    .out_108(digital_vending_machine_circuit_1_out_108), .out_109(digital_vending_machine_circuit_1_out_109),
    .out_85(digital_vending_machine_circuit_1_out_85), .out_86(digital_vending_machine_circuit_1_out_86),
    .out_87(digital_vending_machine_circuit_1_out_87), .out_88(digital_vending_machine_circuit_1_out_88),
    .out_89(digital_vending_machine_circuit_1_out_89), .out_90(digital_vending_machine_circuit_1_out_90),
    .out_91(digital_vending_machine_circuit_1_out_91), .out_92(digital_vending_machine_circuit_1_out_92),
    .out_110(digital_vending_machine_circuit_1_out_110), .out_111(digital_vending_machine_circuit_1_out_111),
    .out_112(digital_vending_machine_circuit_1_out_112), .out_113(digital_vending_machine_circuit_1_out_113),
    .out_114(digital_vending_machine_circuit_1_out_114), .out_115(digital_vending_machine_circuit_1_out_115),
    .out_45(digital_vending_machine_circuit_1_out_45), .out_46(digital_vending_machine_circuit_1_out_46),
    .out_47(digital_vending_machine_circuit_1_out_47), .out_48(digital_vending_machine_circuit_1_out_48),
    .out_49(digital_vending_machine_circuit_1_out_49), .out_50(digital_vending_machine_circuit_1_out_50),
    .out_51(digital_vending_machine_circuit_1_out_51), .out_52(digital_vending_machine_circuit_1_out_52),
    .out_53(digital_vending_machine_circuit_1_out_53), .out_54(digital_vending_machine_circuit_1_out_54),
    .out_55(digital_vending_machine_circuit_1_out_55), .out_56(digital_vending_machine_circuit_1_out_56),
    .out_57(digital_vending_machine_circuit_1_out_57), .out_58(digital_vending_machine_circuit_1_out_58),
    .out_59(digital_vending_machine_circuit_1_out_59), .out_60(digital_vending_machine_circuit_1_out_60),
    .out_61(digital_vending_machine_circuit_1_out_61), .out_62(digital_vending_machine_circuit_1_out_62),
    .out_63(digital_vending_machine_circuit_1_out_63), .out_64(digital_vending_machine_circuit_1_out_64),
    .out_65(digital_vending_machine_circuit_1_out_65), .out_66(digital_vending_machine_circuit_1_out_66),
    .out_67(digital_vending_machine_circuit_1_out_67), .out_68(digital_vending_machine_circuit_1_out_68),
    .out_69(digital_vending_machine_circuit_1_out_69), .out_70(digital_vending_machine_circuit_1_out_70),
    .out_71(digital_vending_machine_circuit_1_out_71), .out_72(digital_vending_machine_circuit_1_out_72),
    .out_73(digital_vending_machine_circuit_1_out_73), .out_74(digital_vending_machine_circuit_1_out_74),
    .out_75(digital_vending_machine_circuit_1_out_75), .out_76(digital_vending_machine_circuit_1_out_76),
    .out_77(digital_vending_machine_circuit_1_out_77), .out_78(digital_vending_machine_circuit_1_out_78),
    .out_79(digital_vending_machine_circuit_1_out_79), .out_80(digital_vending_machine_circuit_1_out_80),
    .out_93(digital_vending_machine_circuit_1_out_93), .out_94(digital_vending_machine_circuit_1_out_94),
    .out_95(digital_vending_machine_circuit_1_out_95), .out_96(digital_vending_machine_circuit_1_out_96),
    .out_97(digital_vending_machine_circuit_1_out_97), .out_98(digital_vending_machine_circuit_1_out_98),
    .out_99(digital_vending_machine_circuit_1_out_99), .out_100(digital_vending_machine_circuit_1_out_100),
    .out_101(digital_vending_machine_circuit_1_out_101), .out_102(digital_vending_machine_circuit_1_out_102),
    .out_103(digital_vending_machine_circuit_1_out_103), .out_104(digital_vending_machine_circuit_1_out_104),
    .out_105(digital_vending_machine_circuit_1_out_105), .out_106(digital_vending_machine_circuit_1_out_106),
    .out_116(digital_vending_machine_circuit_1_out_116), .out_117(digital_vending_machine_circuit_1_out_117),
    .out_118(digital_vending_machine_circuit_1_out_118), .out_119(digital_vending_machine_circuit_1_out_119),
    .out_120(digital_vending_machine_circuit_1_out_120), .out_121(digital_vending_machine_circuit_1_out_121),
    .out_122(digital_vending_machine_circuit_1_out_122), .out_123(digital_vending_machine_circuit_1_out_123),
    .out_124(digital_vending_machine_circuit_1_out_124), .out_125(digital_vending_machine_circuit_1_out_125),
    .out_126(digital_vending_machine_circuit_1_out_126), .out_127(digital_vending_machine_circuit_1_out_127),
    .out_128(digital_vending_machine_circuit_1_out_128), .out_129(digital_vending_machine_circuit_1_out_129),
    .out_130(digital_vending_machine_circuit_1_out_130), .out_131(digital_vending_machine_circuit_1_out_131),
    .out_132(digital_vending_machine_circuit_1_out_132), .out_133(digital_vending_machine_circuit_1_out_133),
    .out_134(digital_vending_machine_circuit_1_out_134), .out_135(digital_vending_machine_circuit_1_out_135));
  _7_Segment_Display u_7_segment_display_7 (
    .g(digital_vending_machine_circuit_1_out_49), .f(digital_vending_machine_circuit_1_out_50),
    .a(digital_vending_machine_circuit_1_out_51), .b(digital_vending_machine_circuit_1_out_52),
    .e(digital_vending_machine_circuit_1_out_56), .d(digital_vending_machine_circuit_1_out_57),
    .c(digital_vending_machine_circuit_1_out_58));  // open: dp
  _7_Segment_Display u_7_segment_display_8 (
    .g(digital_vending_machine_circuit_1_out_63), .f(digital_vending_machine_circuit_1_out_64),
    .a(digital_vending_machine_circuit_1_out_65), .b(digital_vending_machine_circuit_1_out_66),
    .e(digital_vending_machine_circuit_1_out_70), .d(digital_vending_machine_circuit_1_out_71),
    .c(digital_vending_machine_circuit_1_out_72));  // open: dp
  _7_Segment_Display u_7_segment_display_9 (
    .g(digital_vending_machine_circuit_1_out_77), .f(digital_vending_machine_circuit_1_out_78),
    .a(digital_vending_machine_circuit_1_out_79), .b(digital_vending_machine_circuit_1_out_80),
    .e(digital_vending_machine_circuit_1_out_96), .d(digital_vending_machine_circuit_1_out_97),
    .c(digital_vending_machine_circuit_1_out_98));  // open: dp
  _7_Segment_Display u_7_segment_display_10 (
    .g(digital_vending_machine_circuit_1_out_103), .f(digital_vending_machine_circuit_1_out_104),
    .a(digital_vending_machine_circuit_1_out_105), .b(digital_vending_machine_circuit_1_out_106),
    .e(digital_vending_machine_circuit_1_out_119), .d(digital_vending_machine_circuit_1_out_120),
    .c(digital_vending_machine_circuit_1_out_121));  // open: dp
  _7_Segment_Display u_7_segment_display_11 (
    .g(digital_vending_machine_circuit_1_out_126), .f(digital_vending_machine_circuit_1_out_127),
    .a(digital_vending_machine_circuit_1_out_128), .b(digital_vending_machine_circuit_1_out_129),
    .e(digital_vending_machine_circuit_1_out_133), .d(digital_vending_machine_circuit_1_out_134),
    .c(digital_vending_machine_circuit_1_out_135));  // open: dp
  _7_Segment_Display u_7_segment_display_12 (
    .g(digital_vending_machine_circuit_1_out_89), .f(digital_vending_machine_circuit_1_out_90),
    .a(digital_vending_machine_circuit_1_out_91), .b(digital_vending_machine_circuit_1_out_92),
    .e(digital_vending_machine_circuit_1_out_113), .d(digital_vending_machine_circuit_1_out_114),
    .c(digital_vending_machine_circuit_1_out_115));  // open: dp
  _7_Segment_Display u_7_segment_display_13 (
    .g(digital_vending_machine_circuit_1_out_85), .f(digital_vending_machine_circuit_1_out_86),
    .a(digital_vending_machine_circuit_1_out_87), .b(digital_vending_machine_circuit_1_out_88),
    .e(digital_vending_machine_circuit_1_out_110), .d(digital_vending_machine_circuit_1_out_111),
    .c(digital_vending_machine_circuit_1_out_112));  // open: dp
  _7_Segment_Display u_7_segment_display_14 (
    .g(digital_vending_machine_circuit_1_out_17), .f(digital_vending_machine_circuit_1_out_18),
    .a(digital_vending_machine_circuit_1_out_19), .b(digital_vending_machine_circuit_1_out_20),
    .e(digital_vending_machine_circuit_1_out_25), .d(digital_vending_machine_circuit_1_out_26),
    .c(digital_vending_machine_circuit_1_out_27));  // open: dp
  _7_Segment_Display u_7_segment_display_15 (
    .g(digital_vending_machine_circuit_1_out_31), .f(digital_vending_machine_circuit_1_out_32),
    .a(digital_vending_machine_circuit_1_out_33), .b(digital_vending_machine_circuit_1_out_34),
    .e(digital_vending_machine_circuit_1_out_39), .d(digital_vending_machine_circuit_1_out_40),
    .c(digital_vending_machine_circuit_1_out_41));  // open: dp
  _7_Segment_Display u_7_segment_display_16 (
    .g(digital_vending_machine_circuit_1_out_21), .f(digital_vending_machine_circuit_1_out_22),
    .a(digital_vending_machine_circuit_1_out_23), .b(digital_vending_machine_circuit_1_out_24),
    .e(digital_vending_machine_circuit_1_dollar), .d(digital_vending_machine_circuit_1_out_29),
    .c(digital_vending_machine_circuit_1_out_30));  // open: dp
  _7_Segment_Display u_7_segment_display_17 (
    .g(digital_vending_machine_circuit_1_out_35), .f(digital_vending_machine_circuit_1_out_36),
    .a(digital_vending_machine_circuit_1_out_37), .b(digital_vending_machine_circuit_1_out_38),
    .e(digital_vending_machine_circuit_1_dollar_2), .d(digital_vending_machine_circuit_1_out_43),
    .c(digital_vending_machine_circuit_1_out_44));  // open: dp
  Button _1 (.out(_1_out));
  Button _2 (.out(_2_out));
  Button _5 (.out(_5_out));
  Button _10 (.out(_10_out));
  Button Cancel (.out(Cancel_out));
  Button A__2 (.out(A__2_out));
  Button B__3 (.out(B__3_out));
  Button C__6 (.out(C__6_out));
  Button D__8 (.out(D__8_out));
  Button E__12 (.out(E__12_out));
  Button Take_Return___Product (.out(Take_Return___Product_out));

  // Notes on the sheet:
  //   A
  //   B
  //   C
  //   D
  //   E
  //   Product
  //   Return
  //   Dollar Inserted
  //   Dollar Needed
endmodule

module _4_bit_Asynchronous_Down_Counter (
  input  Clock,
  input  Preset,
  input  Disable,
  output out_4,
  output out_5,
  output out_6,
  output out_7,
  output out_8
);

  wire and_1_out;

  T_Flip_Flop t_ff_1 (.clk(Clock), .T(1'b1), .Q(out_4), .preset(Preset), .en(and_1_out));  // open: Qn, reset
  T_Flip_Flop t_ff_2 (.clk(out_4), .T(1'b1), .Q(out_5), .preset(Preset), .en(and_1_out));  // open: Qn, reset
  T_Flip_Flop t_ff_3 (.clk(out_5), .T(1'b1), .Q(out_6), .preset(Preset), .en(and_1_out));  // open: Qn, reset
  T_Flip_Flop t_ff_4 (.clk(out_6), .T(1'b1), .Q(out_7), .preset(Preset), .en(and_1_out));  // open: Qn, reset
  and and_1 (and_1_out, Disable, out_8);
  or or_1 (out_8, out_4, out_5, out_6, out_7);
endmodule
